# Fritzing sketch ArduinoLCDGame (saved by Fritzing 0.9.2b)
breadboards: 1

parts:
  Part1 = Arduino Uno (Rev3)
  LCD1 = LCD screen
  R1 = Resistor [tolerance=±5% resistance=220 package=THT]
  R2 = Trimmer Potentiometer [maximum_resistance=10kΩ package=THT]
  S1 = Pushbutton [package="[THT]"]

nets:
  N1: Part1.D9_PWM, LCD1.E
  N2: Part1.D10_PWM/SS, LCD1.R/W
  N3: Part1.D11_PWM/MOSI, LCD1.RS
  N4: Part1.D2, S1.Pin_1, S1.Pin_2
  N5: Part1.D3_PWM, LCD1.DB6
  N6: Part1.D4, LCD1.DB5
  N7: Part1.D5_PWM, LCD1.DB4
  N8: Part1.D6_PWM, LCD1.DB3
  5V: Part1.5V, LCD1.VDD, LCD1.DB2, R1.Pin_0, R2.leg2
  GND: Part1.GND, LCD1.VSS, LCD1.LED-, R2.leg1, S1.Pin_3, S1.Pin_4
  N9: LCD1.V0, R2.wiper
  N10: LCD1.LED+, R1.Pin_1
